// Logisim project 4BIT_COMPUTING_DEVICE.circ as structural Verilog: 1 circuit, main circuit main
module main (
  input  [3:0] in_1,
  input  [3:0] in_2,
  input  [3:0] in_3,
  input  [4:0] in_4,
  input  [4:0] in_5,
  output [3:0] out_6,
  output [3:0] out_7,
  output [3:0] out_8,
  output [3:0] out_9,
  output [3:0] out_10,
  output [3:0] out_11,
  output [3:0] out_12
);

  wire main_4_out_14, main_5_out_11, main_5_out_12, main_5_out_13, main_5_out_14, main_6_out_11,
       main_6_out_12, main_6_out_13, main_6_out_14, main_7_out_11, main_7_out_12, main_7_out_13,
       main_7_out_14, main_8_out_11, main_8_out_12, main_8_out_13, main_8_out_14, main_9_out_11,
       main_9_out_12, main_9_out_13, main_9_out_14, main_10_out_11, main_10_out_12, main_10_out_13,
       main_10_out_14, main_11_out_11, main_11_out_12, main_11_out_13, main_11_out_14, main_12_out_11,
       main_12_out_12, main_12_out_13, main_12_out_14, main_13_out_11, main_13_out_12, main_13_out_13,
       main_13_out_14, main_14_out_11, main_14_out_12, main_14_out_13, main_14_out_14, main_15_out_11,
       main_15_out_12, main_15_out_13, main_15_out_14, main_16_out_11, main_16_out_12, main_16_out_13,
       main_16_out_14, main_18_out_11, main_18_out_12, main_18_out_13, main_18_out_14, main_19_out_11,
       main_19_out_12, main_19_out_13, main_19_out_14, main_20_out_11, main_20_out_12, main_20_out_13,
       main_20_out_14, main_21_out_11, main_21_out_12, main_21_out_13, main_21_out_14, main_22_out_11,
       main_22_out_12, main_22_out_13, main_22_out_14, main_23_out_11, main_23_out_12, main_23_out_13,
       main_23_out_14, main_24_out_11, main_24_out_12, main_24_out_13, main_24_out_14, main_25_out_11,
       main_25_out_12, main_25_out_13, main_25_out_14;

  _7408_AND_main main_1 (
    .in_2(in_4[4]), .in_3(in_1[0]), .out_11(out_6[0]), .in_4(in_4[4]), .in_5(in_1[1]), .out_12(out_6[1]),
    .in_6(in_4[4]), .in_7(in_1[3]), .out_13(out_6[3]), .in_8(in_4[4]), .in_9(in_1[2]), .out_14(out_6[2]));  // open: GND, Vcc
  _7408_AND_main main_2 (
    .in_2(in_4[4]), .in_3(in_2[0]), .out_11(out_7[0]), .in_4(in_4[4]), .in_5(in_2[1]), .out_12(out_7[1]),
    .in_6(in_4[4]), .in_7(in_2[3]), .out_13(out_7[3]), .in_8(in_4[4]), .in_9(in_2[2]), .out_14(out_7[2]));  // open: GND, Vcc
  _7408_AND_main main_3 (
    .in_2(in_4[4]), .in_3(in_3[0]), .out_11(out_8[0]), .in_4(in_4[4]), .in_5(in_3[1]), .out_12(out_8[1]),
    .in_6(in_4[4]), .in_7(in_3[3]), .out_13(out_8[3]), .in_8(in_4[4]), .in_9(in_3[2]), .out_14(out_8[2]));  // open: GND, Vcc
  _7404_NOT_main main_4 (
    .in_7(main_5_out_11), .out_14(main_4_out_14));  // open: in_2, in_3, out_9, in_4, out_10, in_8, in_1, in_5, in_6, out_12, out_13, out_11
  _7408_AND_main main_5 (
    .in_2(in_3[0]), .in_3(main_5_out_12), .out_11(main_5_out_11), .in_4(in_3[1]), .in_5(main_5_out_14),
    .out_12(main_5_out_12), .in_6(1'b1), .in_7(in_3[3]), .out_13(main_5_out_13), .in_8(main_5_out_13),
    .in_9(in_3[2]), .out_14(main_5_out_14));  // open: GND, Vcc
  _7408_AND_main main_6 (
    .in_2(main_4_out_14), .in_3(in_1[0]), .out_11(main_6_out_11), .in_4(main_4_out_14), .in_5(in_1[1]),
    .out_12(main_6_out_12), .in_6(main_4_out_14), .in_7(in_1[3]), .out_13(main_6_out_13),
    .in_8(main_4_out_14), .in_9(in_1[2]), .out_14(main_6_out_14));  // open: GND, Vcc
  _7432_OR_main main_7 (
    .in_2(in_3[0]), .in_3(in_2[0]), .out_11(main_7_out_11), .in_4(in_3[1]), .in_5(in_2[1]),
    .out_12(main_7_out_12), .in_6(in_3[3]), .in_7(in_2[3]), .out_13(main_7_out_13), .in_8(in_3[2]),
    .in_9(in_2[2]), .out_14(main_7_out_14));  // open: GND, Vcc
  _7432_OR_main main_8 (
    .in_2(in_1[0]), .in_3(in_3[0]), .out_11(main_8_out_11), .in_4(in_1[1]), .in_5(in_3[1]),
    .out_12(main_8_out_12), .in_6(in_1[3]), .in_7(in_3[3]), .out_13(main_8_out_13), .in_8(in_1[2]),
    .in_9(in_3[2]), .out_14(main_8_out_14));  // open: GND, Vcc
  _7432_OR_main main_9 (
    .in_2(in_1[0]), .in_3(in_2[0]), .out_11(main_9_out_11), .in_4(in_1[1]), .in_5(in_2[1]),
    .out_12(main_9_out_12), .in_6(in_1[3]), .in_7(in_2[3]), .out_13(main_9_out_13), .in_8(in_1[2]),
    .in_9(in_2[2]), .out_14(main_9_out_14));  // open: GND, Vcc
  _7432_OR_main main_10 (
    .in_2(in_1[0]), .in_3(in_2[0]), .out_11(main_10_out_11), .in_4(in_1[1]), .in_5(in_2[1]),
    .out_12(main_10_out_12), .in_6(in_1[3]), .in_7(in_2[3]), .out_13(main_10_out_13), .in_8(in_1[2]),
    .in_9(in_2[2]), .out_14(main_10_out_14));  // open: GND, Vcc
  _7486_XOR_main main_11 (
    .in_2(in_1[0]), .in_3(in_2[0]), .out_11(main_11_out_11), .in_4(in_1[1]), .in_5(in_2[1]),
    .out_12(main_11_out_12), .in_6(in_1[3]), .in_7(in_2[3]), .out_13(main_11_out_13), .in_8(in_1[2]),
    .in_9(in_2[2]), .out_14(main_11_out_14));  // open: GND, Vcc
  _7402_NOR_main main_12 (
    .in_3(in_1[0]), .in_2(in_2[0]), .out_11(main_12_out_11), .in_5(in_2[1]), .in_4(in_1[1]),
    .out_12(main_12_out_12), .in_7(in_1[3]), .in_6(in_2[3]), .out_13(main_12_out_13), .GND(in_1[2]),
    .in_8(in_2[2]), .out_14(main_12_out_14));  // open: in_10, Vcc
  _7432_OR_main main_13 (
    .in_2(in_1[0]), .in_3(in_2[0]), .out_11(main_13_out_11), .in_4(in_1[1]), .in_5(in_2[1]),
    .out_12(main_13_out_12), .in_6(in_1[3]), .in_7(in_2[3]), .out_13(main_13_out_13), .in_8(in_1[2]),
    .in_9(in_2[2]), .out_14(main_13_out_14));  // open: GND, Vcc
  _7408_AND_main main_14 (
    .in_2(in_1[0]), .in_3(in_2[0]), .out_11(main_14_out_11), .in_4(in_1[1]), .in_5(in_2[1]),
    .out_12(main_14_out_12), .in_6(in_1[3]), .in_7(in_2[3]), .out_13(main_14_out_13), .in_8(in_1[2]),
    .in_9(in_2[2]), .out_14(main_14_out_14));  // open: GND, Vcc
  _7408_AND_main main_15 (
    .in_2(main_5_out_11), .in_3(in_2[0]), .out_11(main_15_out_11), .in_4(main_5_out_11), .in_5(in_2[1]),
    .out_12(main_15_out_12), .in_6(main_5_out_11), .in_7(in_2[3]), .out_13(main_15_out_13),
    .in_8(main_5_out_11), .in_9(in_2[2]), .out_14(main_15_out_14));  // open: GND, Vcc
  _7432_OR_main main_16 (
    .in_2(main_6_out_11), .in_3(main_15_out_11), .out_11(main_16_out_11), .in_4(main_15_out_12),
    .in_5(main_6_out_12), .out_12(main_16_out_12), .in_6(main_6_out_13), .in_7(main_15_out_13),
    .out_13(main_16_out_13), .in_8(main_6_out_14), .in_9(main_15_out_14), .out_14(main_16_out_14));  // open: GND, Vcc
  _7408_AND_main main_17 (
    .in_2(main_16_out_11), .in_3(in_4[3]), .out_11(out_12[0]), .in_4(main_16_out_12), .in_5(in_4[3]),
    .out_12(out_12[1]), .in_6(in_4[3]), .in_7(main_16_out_13), .out_13(out_12[3]), .in_8(in_4[3]),
    .in_9(main_16_out_14), .out_14(out_12[2]));  // open: GND, Vcc
  _7408_AND_main main_18 (
    .in_2(main_7_out_11), .in_3(in_4[2]), .out_11(main_18_out_11), .in_4(main_7_out_12), .in_5(in_4[2]),
    .out_12(main_18_out_12), .in_6(main_7_out_13), .in_7(in_4[2]), .out_13(main_18_out_13),
    .in_8(main_7_out_14), .in_9(in_4[2]), .out_14(main_18_out_14));  // open: GND, Vcc
  _7408_AND_main main_19 (
    .in_2(main_8_out_11), .in_3(in_4[1]), .out_11(main_19_out_11), .in_4(main_8_out_12), .in_5(in_4[1]),
    .out_12(main_19_out_12), .in_6(main_8_out_13), .in_7(in_4[1]), .out_13(main_19_out_13),
    .in_8(main_8_out_14), .in_9(in_4[1]), .out_14(main_19_out_14));  // open: GND, Vcc
  _7408_AND_main main_20 (
    .in_2(main_9_out_11), .in_3(in_4[0]), .out_11(main_20_out_11), .in_4(main_9_out_12), .in_5(in_4[0]),
    .out_12(main_20_out_12), .in_6(main_9_out_13), .in_7(in_4[0]), .out_13(main_20_out_13),
    .in_8(main_9_out_14), .in_9(in_4[0]), .out_14(main_20_out_14));  // open: GND, Vcc
  _7408_AND_main main_21 (
    .in_2(main_10_out_11), .in_3(in_5[4]), .out_11(main_21_out_11), .in_4(main_10_out_12), .in_5(in_5[4]),
    .out_12(main_21_out_12), .in_6(main_10_out_13), .in_7(in_5[4]), .out_13(main_21_out_13),
    .in_8(main_10_out_14), .in_9(in_5[4]), .out_14(main_21_out_14));  // open: GND, Vcc
  _7408_AND_main main_22 (
    .in_2(main_11_out_11), .in_3(in_5[3]), .out_11(main_22_out_11), .in_4(main_11_out_12), .in_5(in_5[3]),
    .out_12(main_22_out_12), .in_6(main_11_out_13), .in_7(in_5[3]), .out_13(main_22_out_13),
    .in_8(main_11_out_14), .in_9(in_5[3]), .out_14(main_22_out_14));  // open: GND, Vcc
  _7408_AND_main main_23 (
    .in_2(main_12_out_11), .in_3(in_5[2]), .out_11(main_23_out_11), .in_4(main_12_out_12), .in_5(in_5[2]),
    .out_12(main_23_out_12), .in_6(main_12_out_13), .in_7(in_5[2]), .out_13(main_23_out_13),
    .in_8(main_12_out_14), .in_9(in_5[2]), .out_14(main_23_out_14));  // open: GND, Vcc
  _7408_AND_main main_24 (
    .in_2(main_13_out_11), .in_3(in_5[1]), .out_11(main_24_out_11), .in_4(main_13_out_12), .in_5(in_5[1]),
    .out_12(main_24_out_12), .in_6(main_13_out_13), .in_7(in_5[1]), .out_13(main_24_out_13),
    .in_8(main_13_out_14), .in_9(in_5[1]), .out_14(main_24_out_14));  // open: GND, Vcc
  _7408_AND_main main_25 (
    .in_2(main_14_out_11), .in_3(in_5[0]), .out_11(main_25_out_11), .in_4(main_14_out_12), .in_5(in_5[0]),
    .out_12(main_25_out_12), .in_6(main_14_out_13), .in_7(in_5[0]), .out_13(main_25_out_13),
    .in_8(main_14_out_14), .in_9(in_5[0]), .out_14(main_25_out_14));  // open: GND, Vcc
  DIODE_main main_26 (.in_1(main_18_out_11), .out_2(out_9[0]));
  DIODE_main main_27 (.in_1(main_18_out_12), .out_2(out_9[1]));
  DIODE_main main_28 (.in_1(main_18_out_14), .out_2(out_9[2]));
  DIODE_main main_29 (.in_1(main_18_out_13), .out_2(out_9[3]));
  DIODE_main main_30 (.in_1(main_19_out_11), .out_2(out_10[0]));
  DIODE_main main_31 (.in_1(main_19_out_12), .out_2(out_10[1]));
  DIODE_main main_32 (.in_1(main_19_out_14), .out_2(out_10[2]));
  DIODE_main main_33 (.in_1(main_19_out_13), .out_2(out_10[3]));
  DIODE_main main_34 (.in_1(main_20_out_11));  // open: out_2
  DIODE_main main_35 (.in_1(main_20_out_12), .out_2(out_11[0]));
  DIODE_main main_36 (.in_1(main_20_out_14), .out_2(out_11[1]));
  DIODE_main main_37 (.in_1(main_20_out_13), .out_2(out_11[2]));
  DIODE_main main_38 (.in_1(main_21_out_11), .out_2(out_11[1]));
  DIODE_main main_39 (.in_1(main_21_out_12), .out_2(out_11[2]));
  DIODE_main main_40 (.in_1(main_21_out_14), .out_2(out_11[3]));
  DIODE_main main_41 (.in_1(main_21_out_13));  // open: out_2
  DIODE_main main_42 (.in_1(main_22_out_11), .out_2(out_11[0]));
  DIODE_main main_43 (.in_1(main_22_out_12), .out_2(out_11[1]));
  DIODE_main main_44 (.in_1(main_22_out_14), .out_2(out_11[2]));
  DIODE_main main_45 (.in_1(main_22_out_13), .out_2(out_11[3]));
  DIODE_main main_46 (.in_1(main_23_out_11), .out_2(out_11[0]));
  DIODE_main main_47 (.in_1(main_23_out_12), .out_2(out_11[1]));
  DIODE_main main_48 (.in_1(main_23_out_14), .out_2(out_11[2]));
  DIODE_main main_49 (.in_1(main_23_out_13), .out_2(out_11[3]));
  DIODE_main main_50 (.in_1(main_24_out_11), .out_2(out_11[0]));
  DIODE_main main_51 (.in_1(main_24_out_12), .out_2(out_11[1]));
  DIODE_main main_52 (.in_1(main_24_out_14), .out_2(out_11[2]));
  DIODE_main main_53 (.in_1(main_24_out_13), .out_2(out_11[3]));
  DIODE_main main_54 (.in_1(main_25_out_11), .out_2(out_11[0]));
  DIODE_main main_55 (.in_1(main_25_out_12), .out_2(out_11[1]));
  DIODE_main main_56 (.in_1(main_25_out_14), .out_2(out_11[2]));
  DIODE_main main_57 (.in_1(main_25_out_13), .out_2(out_11[3]));
endmodule
