// Logisim project testing ram.circ as structural Verilog: 1 circuit, main circuit main
module main (
  input  [3:0] in_1,
  input  CS,
  input  WE,
  input  [3:0] in_4,
  output [3:0] out_5
);

  _74189_RAM_main main_1 (
    .in_2(in_1[1]), .in_3(in_1[2]), .out_16(out_5[1]), .in_4(in_1[3]), .in_5(in_4[3]), .out_13(out_5[3]),
    .in_7(in_1[0]), .CS(CS), .in_9(in_4[0]), .in_10(in_4[1]), .out_15(out_5[0]), .WE(WE), .in_6(in_4[2]),
    .out_14(out_5[2]));  // open: in_12, Vcc
endmodule
